# Fritzing sketch schematic (saved by Fritzing 0.9.3b)

parts:
  Raspberry_Pi_1 = Raspberry Pi 3 [part_number=RPI-3-V1.2]
  Part1 = Adafruit ADS1115 16Bit I2C ADC [part_number="Adafruit #1085"]
  SONAR1 = Maxbotix MaxSonar Ultrasonic Sensor
  U1 = RJ45 Jack [package=rj45-8]
  U2 = RJ45 Jack [package=rj45-8]
  Part2 = LIDAR-Lite
  Raspberry_Pi_Zero1 = Raspberry Pi Zero
  U3 = RJ45 Jack [package=rj45-8]
  U4 = RJ45 Jack [package=rj45-8]

nets:
  N1: Raspberry_Pi_1.GPIO2, Part1.SDA
  N2: Raspberry_Pi_1.GPIO3, Part1.SCL
  GND: Raspberry_Pi_1.GND, Part1.GND, U1.2, U1.4, U1.6, U1.8
  5V: Raspberry_Pi_1.5V, Part1.VDD, U1.5
  N3: Part1.AIN0, U1.1
  N4: SONAR1.GND, U2.2, U2.4, U2.6, U2.8
  N5: SONAR1.+5V, U2.5
  N6: SONAR1.TX, U2.3
  N7: SONAR1.RX, U2.7
  N8: SONAR1.AN, U2.1
  N9: Part2.5V, U4.5
  N10: Part2.SCL, U4.1
  N11: Part2.SDA, U4.3
  N12: Part2.GND, U4.4
  N13: Raspberry_Pi_Zero1.GPIO2, U3.3
  N14: Raspberry_Pi_Zero1.GPIO3, U3.1
  N15: Raspberry_Pi_Zero1.GND, U3.4
  N16: Raspberry_Pi_Zero1.5V, U3.5

custom parts:
  Adafruit ADS1115 16Bit I2C ADC: For microcontrollers without an analog-to-digital converter or when you want a higher-precision ADC, the ADS1115 provides 16-bit precision at 860 samples/second over I2C. The chip can be configured as 4 single-ended input channels, or two differential channels. As a nice bonus, it even includes a programmable gain amplifier, up to x16, to help boost up smaller single/differential signals to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
  Maxbotix MaxSonar Ultrasonic Sensor: Maxbotix MaxSonar Ultrasonic Sensor LV-EZ0, LV-EZ1, LV-EZ2, LV-EZ3, LV-EZ4
  LIDAR-Lite: PulsedLight LIDAR-Lite Sensor
